# Fritzing sketch Fritzing Sketch David (saved by Fritzing 0.9.3b)
breadboards: 1

parts:
  IC1 = sparkfun_sensors_ad8232 [part_number=SEN-12650 chip_label=IC]
  Part1 = Photon

nets:
  N1: IC1.connector1, Part1.GND
  N2: IC1.connector2, Part1.3V3
  N3: IC1.connector3, Part1.A0
  N4: IC1.connector4, Part1.D0
  N5: IC1.connector5, Part1.D1
